// Logisim project CPU.circ as structural Verilog
module _74181_ALU (
  input  s3,
  input  s2,
  input  s1,
  input  s0,
  input  B3,
  input  a3,
  input  b2,
  input  a2,
  input  b1,
  input  a1,
  input  b0,
  input  a0,
  input  M,
  input  Cn,
  output G,
  output Cn4,
  output P,
  output F3,
  output F2,
  output equ,
  output F1,
  output F0
);

  wire and_1_out, and_2_out, and_3_out, and_4_out, and_5_out, and_6_out, and_7_out, and_8_out, and_9_out,
       and_10_out, and_11_out, and_12_out, and_13_out, and_14_out, and_15_out, and_16_out, and_17_out,
       and_18_out, and_19_out, and_20_out, and_21_out, and_22_out, and_23_out, and_24_out, and_25_out,
       and_26_out, and_27_out, and_28_out, and_29_out, and_30_out, and_31_out, and_32_out, nand_1_out,
       nand_3_out, nor_1_out, nor_2_out, nor_3_out, nor_4_out, nor_5_out, nor_6_out, nor_7_out, nor_8_out,
       nor_10_out, nor_11_out, nor_12_out, not_1_out, not_2_out, not_3_out, not_4_out, not_5_out, not_6_out,
       not_7_out, not_8_out, not_9_out, not_10_out, not_11_out;

  not not_1 (not_1_out, B3);
  not not_2 (not_2_out, b2);
  not not_3 (not_3_out, b1);
  not not_4 (not_4_out, b0);
  and and_1 (and_1_out, B3, s3, a3);
  and and_2 (and_2_out, a3, s2, not_1_out);
  and and_3 (and_3_out, not_1_out, s1);
  and and_4 (and_4_out, B3, s0);
  and and_5 (and_5_out, b2, s3, a2);
  and and_6 (and_6_out, a2, s2, not_2_out);
  and and_7 (and_7_out, not_2_out, s1);
  and and_8 (and_8_out, b2, s0);
  and and_9 (and_9_out, b1, s3, a1);
  and and_10 (and_10_out, a1, s2, not_3_out);
  and and_11 (and_11_out, not_3_out, s1);
  and and_12 (and_12_out, b1, s0);
  and and_13 (and_13_out, b0, s3, a0);
  and and_14 (and_14_out, a0, s2, not_4_out);
  and and_15 (and_15_out, not_4_out, s1);
  and and_16 (and_16_out, b0, s0);
  nor nor_1 (nor_1_out, and_1_out, and_2_out);
  nor nor_2 (nor_2_out, and_3_out, and_4_out, a3);
  nor nor_3 (nor_3_out, and_5_out, and_6_out);
  nor nor_4 (nor_4_out, and_7_out, and_8_out, a2);
  nor nor_5 (nor_5_out, and_9_out, and_10_out);
  nor nor_6 (nor_6_out, and_11_out, and_12_out, a1);
  nor nor_7 (nor_7_out, and_13_out, and_14_out);
  nor nor_8 (nor_8_out, and_15_out, and_16_out, a0);
  not not_5 (not_5_out, M);
  and and_17 (and_17_out, nor_1_out, nor_4_out);
  and and_18 (and_18_out, nor_1_out, nor_3_out, nor_6_out);
  and and_19 (and_19_out, nor_1_out, nor_3_out, nor_5_out, nor_8_out);
  not not_6 (not_6_out, nor_2_out);
  and and_20 (and_20_out, nor_3_out, nor_5_out, nor_7_out, Cn, not_5_out);
  and and_21 (and_21_out, nor_3_out, nor_5_out, nor_8_out, not_5_out);
  and and_22 (and_22_out, nor_3_out, nor_6_out, not_5_out);
  and and_23 (and_23_out, nor_4_out, not_5_out);
  not not_7 (not_7_out, nor_4_out);
  and and_24 (and_24_out, nor_5_out, nor_7_out, Cn, not_5_out);
  and and_25 (and_25_out, nor_5_out, nor_8_out, not_5_out);
  and and_26 (and_26_out, nor_6_out, not_5_out);
  not not_8 (not_8_out, nor_6_out);
  and and_27 (and_27_out, Cn, nor_7_out, not_5_out);
  and and_28 (and_28_out, nor_8_out, not_5_out);
  not not_9 (not_9_out, nor_8_out);
  nand nand_1 (nand_1_out, nor_1_out, nor_3_out, nor_5_out, nor_7_out, Cn);
  nand nand_2 (P, nor_7_out, nor_5_out, nor_3_out, nor_1_out);
  nand nand_3 (nand_3_out, not_5_out, Cn);
  nor nor_9 (G, nor_2_out, and_17_out, and_18_out, and_19_out);
  and and_29 (and_29_out, nor_1_out, not_6_out);
  nor nor_10 (nor_10_out, and_20_out, and_21_out, and_22_out, and_23_out);
  and and_30 (and_30_out, nor_3_out, not_7_out);
  nor nor_11 (nor_11_out, and_24_out, and_25_out, and_26_out);
  and and_31 (and_31_out, nor_5_out, not_8_out);
  nor nor_12 (nor_12_out, and_27_out, and_28_out);
  and and_32 (and_32_out, nor_7_out, not_9_out);
  not not_10 (not_10_out, G);
  not not_11 (not_11_out, nand_1_out);
  xor xor_1 (F3, and_29_out, nor_10_out);
  xor xor_2 (F2, and_30_out, nor_11_out);
  xor xor_3 (F1, and_31_out, nor_12_out);
  xor xor_4 (F0, and_32_out, nand_3_out);
  or or_1 (Cn4, not_10_out, not_11_out);
  and and_33 (equ, F2, F3, F1, F0);
endmodule

module ALU_8B_Extended (
  input  [7:0] A,
  input  [7:0] B,
  input  Cn,
  input  M,
  input  [3:0] S,
  output [7:0] R,
  output Cn8,
  output EQU,
  output A_B,
  output Zero
);

  wire n74181_alu_1_cn4, n74181_alu_1_equ, n74181_alu_2_cn4, n74181_alu_2_equ, n74688_8b_comparator_1_p_q,
       not_1_out;

  not not_1 (not_1_out, Cn);
  _74181_ALU u_74181_alu_1 (
    .s0(S[0]), .s1(S[1]), .s2(S[2]), .s3(S[3]), .B3(B[7]), .Cn4(n74181_alu_1_cn4), .a3(A[7]), .b2(B[6]),
    .F3(R[7]), .a2(A[6]), .b1(B[5]), .F2(R[6]), .equ(n74181_alu_1_equ), .a1(A[5]), .b0(B[4]), .F1(R[5]),
    .F0(R[4]), .a0(A[4]), .M(M), .Cn(n74181_alu_2_cn4));  // open: G, P
  _74181_ALU u_74181_alu_2 (
    .s0(S[0]), .s1(S[1]), .s2(S[2]), .s3(S[3]), .B3(B[3]), .Cn4(n74181_alu_2_cn4), .a3(A[3]), .b2(B[2]),
    .F3(R[3]), .a2(A[2]), .b1(B[1]), .F2(R[2]), .equ(n74181_alu_2_equ), .a1(A[1]), .b0(B[0]), .F1(R[1]),
    .F0(R[0]), .a0(A[0]), .M(M), .Cn(not_1_out));  // open: G, P
  _74688_8B_Comparator u_74688_8b_comparator_1 (.OE(1'b0), .A(A), .B(B), .P_Q(n74688_8b_comparator_1_p_q));
  and and_1 (EQU, n74181_alu_1_equ, n74181_alu_2_equ);
  not not_2 (A_B, n74688_8b_comparator_1_p_q);
  not not_3 (Cn8, n74181_alu_1_cn4);
  nor nor_1 (Zero, R[0], R[1], R[2], R[3], R[4], R[5], R[6], R[7]);

  // Notes on the sheet:
  //   Higher
  //   Lower
endmodule

module _74688_8B_Comparator (
  input  OE,
  input  [7:0] A,
  input  [7:0] B,
  output P_Q
);

  wire and_1_out, not_1_out;
  wire [7:0] xnor_1_out;

  assign xnor_1_out = ~(A ^ B);  // XNOR_Gate xnor_1, 8 bits wide
  and and_1 (and_1_out, xnor_1_out[0], xnor_1_out[1], xnor_1_out[2], xnor_1_out[3], xnor_1_out[4], xnor_1_out[5], xnor_1_out[6], xnor_1_out[7]);
  not not_1 (not_1_out, OE);
  nand nand_1 (P_Q, not_1_out, and_1_out);
endmodule

module _74374_8B_Reg_TS (
  input  [7:0] D,
  input  CLK,
  input  RST,
  input  minus_OE,
  output [7:0] Q
);

  wire not_1_out;
  wire [7:0] register_1_q;

  Register register_1 (.D(D), .en(1'b1), .Q(register_1_q), .clk(CLK), .clr(RST));
  not not_1 (not_1_out, minus_OE);
  assign Q = not_1_out ? register_1_q : 8'bz;  // Controlled_Buffer controlled_buffer_1
endmodule

module Interface_8B (
  input  O_RW,
  input  Isolate,
  input  [7:0] O_In,
  input  [7:0] I_In,
  input  I_RW,
  input  Done,
  input  Start,
  input  RST,
  input  CLK,
  output [7:0] O_Out,
  output [7:0] I_out,
  output [7:0] SEN,
  output Z
);

  wire nand_1_out, nand_2_out, nand_3_out, nand_4_out, nand_5_out, nand_6_out, nand_7_out, nand_8_out,
       nand_9_out, nand_10_out, not_1_out, not_2_out, not_3_out, not_4_out, not_5_out, not_6_out, not_7_out;
  wire [7:0] buffer_8b_nts_1_q;

  not not_1 (not_1_out, Done);
  not not_2 (not_2_out, Z);
  not not_3 (not_3_out, O_RW);
  nand nand_1 (nand_1_out, O_RW, not_2_out);
  nand nand_2 (nand_2_out, Z, I_RW);
  nand nand_3 (nand_3_out, not_1_out, Z);
  nand nand_4 (nand_4_out, not_1_out, Start);
  nand nand_5 (nand_5_out, Start, not_2_out);
  nand nand_6 (nand_6_out, not_3_out, not_2_out);
  nand nand_7 (nand_7_out, nand_1_out, nand_2_out);
  not not_4 (not_4_out, I_RW);
  Register #(.width(1)) register_1 (.D(nand_8_out), .en(1'b1), .Q(Z), .clk(CLK), .clr(RST));
  nand nand_8 (nand_8_out, nand_3_out, nand_4_out, nand_5_out);
  not not_5 (not_5_out, Isolate);
  Buffer_8B_NTS buffer_8b_nts_1 (.D(O_In), .T(nand_6_out), .Q(buffer_8b_nts_1_q));
  Buffer_8B_NTS buffer_8b_nts_2 (.D(I_In), .T(nand_9_out), .Q(buffer_8b_nts_1_q));
  nand nand_9 (nand_9_out, not_4_out, Z);
  nand nand_10 (nand_10_out, nand_6_out, not_5_out);
  Buffer_8B_NTS buffer_8b_nts_3 (.D(SEN), .T(nand_10_out), .Q(O_Out));
  not not_6 (not_6_out, nand_7_out);
  Buffer_8B_NTS buffer_8b_nts_4 (.D(SEN), .T(not_6_out), .Q(buffer_8b_nts_1_q));
  _74374_8B_Reg_TS u_74374_8b_reg_ts_1 (.D(buffer_8b_nts_1_q), .CLK(CLK), .minus_OE(1'b0), .Q(SEN), .RST(RST));
  Buffer_8B_NTS buffer_8b_nts_5 (.D(SEN), .T(Z), .Q(I_out));
  not not_7 (not_7_out, Z);
  _74374_8B_Reg_TS u_74374_8b_reg_ts_2 (.D(SEN), .CLK(CLK), .minus_OE(not_7_out), .Q(I_out), .RST(RST));

  // Notes on the sheet:
  //   0: WRT   1: READ
  //   0: WRT   1: READ
  //   0: Out_CTRL   1: In_CRTL
endmodule

module Buffer_8B_NTS (
  input  [7:0] D,
  input  T,
  output [7:0] Q
);

  wire not_1_out;

  assign Q = not_1_out ? D : 8'bz;  // Controlled_Buffer controlled_buffer_1
  not not_1 (not_1_out, T);
endmodule

module Buffer_NTS (
  input  D,
  input  T,
  output Q
);

  wire not_1_out;

  assign Q = not_1_out ? D : 1'bz;  // Controlled_Buffer controlled_buffer_1
  not not_1 (not_1_out, T);
endmodule

module MC_ALU_8B (
  input  [7:0] DAT,
  input  A_ISO,
  input  A_RW,
  input  SWP,
  input  [7:0] CMD_In,
  input  B_RW,
  input  Start,
  input  CMD_ISO,
  input  CMD_RW,
  input  CLK,
  input  RST,
  output [7:0] DAT_O,
  output [3:0] SEN_ACC0,
  output [3:0] SEN_ACC1,
  output [3:0] SEN_B0,
  output [3:0] SEN_B1,
  output [7:0] CMD_Out,
  output Z,
  output [3:0] Flag,
  output Done
);

  wire alu_8b_extended_1_a_b, and_1_out, buffer_1_out, not_1_out, not_2_out, or_1_out, or_2_out, or_3_out,
       register_1_q;
  wire [1:0] rom_1_data_2;
  wire [3:0] n74157_quad2_1_mux_1_r, n74157_quad2_1_mux_2_r, rom_1_data;
  wire [7:0] alu_8b_extended_1_r, buffer_8b_nts_2_q, interface_8b_1_i_out, interface_8b_2_i_out,
       interface_8b_3_i_out, reg_8b_rw_1_q_2;
  wire [14:6] rom_1_data_3;

  and and_1 (and_1_out, Start, not_1_out);
  not not_1 (not_1_out, register_1_q);
  Register #(.width(1)) register_1 (.D(RST), .en(1'b1), .Q(register_1_q), .clk(or_1_out), .clr(1'b0));
  or or_1 (or_1_out, buffer_1_out, CLK);
  buf buffer_1 (buffer_1_out, RST);
  not not_2 (not_2_out, SWP);
  Interface_8B interface_8b_1 (
    .O_RW(CMD_RW), .Isolate(CMD_ISO), .O_In(CMD_In), .I_In({8{1'b0}}), .I_RW(1'b1), .Done(Done),
    .Start(and_1_out), .RST(RST), .CLK(CLK),
    .I_out({{2{interface_8b_1_i_out[7]}}, interface_8b_1_i_out[5:0]}), .Z(Z), .O_Out(CMD_Out));  // open: SEN
  or or_2 (or_2_out, A_RW, not_2_out, B_RW);
  Buffer_8B_NTS buffer_8b_nts_1 (.D(interface_8b_3_i_out), .T(or_2_out), .Q(DAT));
  _74157_Quad2_1_MUX u_74157_quad2_1_mux_1 (
    .S(rom_1_data_3[12]), .A({{2{interface_8b_1_i_out[7]}}, interface_8b_1_i_out[5:4]}),
    .B({{2{interface_8b_1_i_out[7]}}, rom_1_data_2}), .R(n74157_quad2_1_mux_1_r));
  _74157_Quad2_1_MUX u_74157_quad2_1_mux_2 (
    .S(rom_1_data_3[12]), .A(interface_8b_1_i_out[3:0]), .B(rom_1_data), .R(n74157_quad2_1_mux_2_r));
  Buffer_8B_NTS buffer_8b_nts_2 (.D(interface_8b_2_i_out), .T(or_2_out), .Q(buffer_8b_nts_2_q));
  or or_3 (or_3_out, and_1_out, rom_1_data_3[12]);
  Interface_8B interface_8b_2 (
    .O_RW(A_RW), .Isolate(A_ISO), .O_In(DAT), .I_In(alu_8b_extended_1_r), .I_RW(rom_1_data_3[13]),
    .Done(Done), .Start(and_1_out), .RST(RST), .CLK(CLK), .I_out(interface_8b_2_i_out), .O_Out(DAT_O),
    .SEN({SEN_ACC1, SEN_ACC0}));  // open: Z
  Interface_8B interface_8b_3 (
    .O_RW(B_RW), .Isolate(1'b0), .O_In(buffer_8b_nts_2_q), .I_In({8{1'b0}}), .I_RW(rom_1_data_3[14]),
    .Done(Done), .Start(and_1_out), .RST(RST), .CLK(CLK), .I_out(interface_8b_3_i_out),
    .O_Out(buffer_8b_nts_2_q), .SEN({SEN_B1, SEN_B0}));  // open: Z
  REG_8B_RW reg_8b_rw_1 (
    .WRT(or_3_out), .Q({n74157_quad2_1_mux_1_r, n74157_quad2_1_mux_2_r}), .READ(1'b1), .CLK(CLK), .RST(RST),
    .Q_2(reg_8b_rw_1_q_2));
  ROM #(.dataWidth(16)) rom_1 (
    .addr(reg_8b_rw_1_q_2),
    .data({Done, rom_1_data_3, rom_1_data[0], rom_1_data[1], rom_1_data[2], rom_1_data[3], rom_1_data_2[0], rom_1_data_2[1]}),
    .sel(1'b1));
  ALU_8B_Extended alu_8b_extended_1 (
    .A(interface_8b_2_i_out), .B(interface_8b_3_i_out), .Cn(rom_1_data_3[11]), .M(rom_1_data_3[10]),
    .S({rom_1_data_3[6], rom_1_data_3[7], rom_1_data_3[8], rom_1_data_3[9]}), .R(alu_8b_extended_1_r),
    .EQU(Flag[2]), .A_B(alu_8b_extended_1_a_b), .Cn8(Flag[1]), .Zero(Flag[0]));
  Register #(.width(1)) register_2 (.D(alu_8b_extended_1_a_b), .en(1'b1), .Q(Flag[3]), .clk(CLK), .clr(RST));
  // also tied to GND on the sheet: interface_8b_1_i_out[7]

  // Notes on the sheet:
  //   contents of rom_1 (hex, n*v repeats v):
  //   d27c da7c d9bc d1bc d83c d3fc db7c d23c ddbc db3c dc3c d33c da7c da7c f9bc 6c3c 48*9a7c
  //   CMD
  //   NXT_ADR
endmodule

module _74157_Quad2_1_MUX (
  input  S,
  input  [3:0] A,
  input  [3:0] B,
  output [3:0] R
);

  Multiplexer #(.enable("false")) multiplexer_1 (.in0(A[0]), .in1(B[0]), .out(R[0]), .sel(S));
  Multiplexer #(.enable("false")) multiplexer_2 (.in0(A[1]), .in1(B[1]), .out(R[1]), .sel(S));
  Multiplexer #(.enable("false")) multiplexer_3 (.in0(A[2]), .in1(B[2]), .out(R[2]), .sel(S));
  Multiplexer #(.enable("false")) multiplexer_4 (.in0(A[3]), .in1(B[3]), .out(R[3]), .sel(S));
endmodule

module REG_8B_RW (
  input  WRT,
  input  [7:0] Q,
  input  READ,
  input  CLK,
  input  RST,
  output [7:0] Q_2
);

  wire not_1_out, not_2_out;
  wire [7:0] buffer_8b_nts_1_q, register_1_q;

  not not_1 (not_1_out, READ);
  not not_2 (not_2_out, WRT);
  Buffer_8B_NTS buffer_8b_nts_1 (.D(Q), .T(not_2_out), .Q(buffer_8b_nts_1_q));
  Buffer_8B_NTS buffer_8b_nts_2 (.D(register_1_q), .T(WRT), .Q(buffer_8b_nts_1_q));
  Register register_1 (.D(buffer_8b_nts_1_q), .en(1'b1), .Q(register_1_q), .clk(CLK), .clr(RST));
  Buffer_8B_NTS buffer_8b_nts_3 (.D(register_1_q), .T(not_1_out), .Q(Q_2));
endmodule

module REG_RW (
  input  WRT,
  input  Q,
  input  READ,
  input  CLK,
  input  RST,
  output Q_2
);

  wire buffer_nts_1_q, not_1_out, not_2_out, register_1_q;

  not not_1 (not_1_out, READ);
  not not_2 (not_2_out, WRT);
  Buffer_NTS buffer_nts_1 (.D(Q), .T(not_2_out), .Q(buffer_nts_1_q));
  Buffer_NTS buffer_nts_2 (.D(register_1_q), .T(WRT), .Q(buffer_nts_1_q));
  Register #(.width(1)) register_1 (.D(buffer_nts_1_q), .en(1'b1), .Q(register_1_q), .clk(CLK), .clr(RST));
  Buffer_NTS buffer_nts_3 (.D(register_1_q), .T(not_1_out), .Q(Q_2));
endmodule

module CU_8B_CRUDE (
  input  M,
  input  CLK,
  input  RST,
  output [7:0] out_4,
  output [7:0] END,
  output [15:0] out_6
);

  wire _6, _7, _8, _10, _14, _15, and_2_out, and_3_out, and_4_out, and_6_out, and_8_out, and_9_out,
       and_10_out, and_12_out, and_13_out, and_14_out, and_15_out, and_16_out, and_17_out, and_18_out,
       and_19_out, and_20_out, and_21_out, and_22_out, and_23_out, BS, buffer_1_out, button_1_out,
       clock_1_out, controlled_buffer_1_out, FT, gpr_ctrl_1_r0_iso, gpr_ctrl_1_r0_rw, gpr_ctrl_1_r1_iso,
       gpr_ctrl_1_r1_rw, JMP, multiplexer_1_out, nand_1_out, nand_2_out, nand_3_out, nand_4_out, nor_1_out,
       nor_2_out, nor_4_out, nor_5_out, nor_6_out, nor_7_out, nor_8_out, not_2_out, not_3_out, not_4_out,
       not_5_out, not_6_out, not_7_out, not_8_out, not_9_out, not_10_out, not_11_out, not_12_out, not_13_out,
       not_14_out, not_16_out, not_17_out, not_18_out, not_19_out, or_1_out, or_2_out, or_4_out, or_5_out,
       or_6_out, or_7_out, or_8_out, PCI, pull_resistor_1_node, register_1_q, register_2_q, register_3_q,
       regpush_4b_1_q0, regpush_4b_1_q1, regpush_4b_1_q2, regpush_4b_2_q0, regpush_4b_2_q1, regpush_4b_2_q2,
       xnor_1_out, xor_1_out, xor_2_out, xor_3_out, xor_4_out;
  wire [3:0] FF, gpreg_8b_1_sen0, gpreg_8b_1_sen1, mc_alu_8b_1_flag, mc_alu_8b_1_sen_acc0,
       mc_alu_8b_1_sen_acc1, mc_alu_8b_1_sen_b0, mc_alu_8b_1_sen_b1, R0, R1;
  wire [6:0] eeprom_8kx16_1_out;
  wire [7:0] AD, buffer_8b_nts_1_q, buffer_8b_nts_3_q, OH, OL;
  wire [7:6] undriven;
  wire [13:6] eeprom_8kx16_1_out_2;
  wire [15:0] buffer_16b_nts_1_q, pull_resistor_6_node, SPB, SPBO;

  REGPUSH_4B regpush_4b_1 (
    .D(pull_resistor_1_node), .CLK(controlled_buffer_1_out), .RST(or_1_out), .Q0(regpush_4b_1_q0),
    .Q1(regpush_4b_1_q1), .Q2(regpush_4b_1_q2));  // open: Q3
  Pull_Resistor pull_resistor_1 (.node(pull_resistor_1_node));
  and and_1 (pull_resistor_1_node, END[7], FT);
  and and_2 (and_2_out, END[6], FT);
  Pull_Resistor pull_resistor_2 (.node(and_2_out));
  or or_1 (or_1_out, and_3_out, RST);
  nor nor_1 (nor_1_out, not_2_out, controlled_buffer_1_out);
  and and_3 (and_3_out, nor_1_out, FT);
  Button button_1 (.out(button_1_out));
  not not_1 (_7, or_2_out);
  or or_2 (or_2_out, regpush_4b_1_q0, regpush_4b_1_q1, regpush_4b_1_q2);
  REGPUSH_4B regpush_4b_2 (
    .D(and_2_out), .CLK(controlled_buffer_1_out), .RST(or_1_out), .Q0(regpush_4b_2_q0), .Q1(regpush_4b_2_q1),
    .Q2(regpush_4b_2_q2));  // open: Q3
  not not_2 (not_2_out, controlled_buffer_1_out);
  assign controlled_buffer_1_out = M ? clock_1_out : 1'bz;  // Controlled_Buffer controlled_buffer_1
  Clock clock_1 (.out(clock_1_out));
  Buffer_NTS buffer_nts_1 (.D(button_1_out), .T(M), .Q(controlled_buffer_1_out));
  and and_4 (and_4_out, xor_1_out, xnor_1_out);
  xor xor_1 (xor_1_out, _15, _14);
  Multiplexer #(.enable("false")) multiplexer_1 (.in0(_6), .in1(or_2_out), .out(multiplexer_1_out), .sel(BS));
  or or_3 (_6, regpush_4b_2_q0, regpush_4b_2_q1, regpush_4b_2_q2);
  not not_3 (not_3_out, eeprom_8kx16_1_out_2[6]);
  xnor xnor_1 (xnor_1_out, _8, _10);
  GPR_CTRL gpr_ctrl_1 (
    .R0_ISO(gpr_ctrl_1_r0_iso), .R0_RW(gpr_ctrl_1_r0_rw), .R1_ISO(gpr_ctrl_1_r1_iso),
    .R1_RW(gpr_ctrl_1_r1_rw), .ENA(and_4_out), .B6(multiplexer_1_out), .F1(_14), .F0(_15));
  Buffer_8B_NTS buffer_8b_nts_1 (.D(END), .T(eeprom_8kx16_1_out_2[11]), .Q(buffer_8b_nts_1_q));
  RAM #(.addrWidth(16)) ram_1 (
    .addr(SPBO), .data(buffer_8b_nts_1_q), .sel(not_3_out), .clk(controlled_buffer_1_out),
    .ld(eeprom_8kx16_1_out_2[11]), .clr(1'b0));
  and and_5 (BS, _10, _8);
  GPREG_8B gpreg_8b_1 (
    .ISO(gpr_ctrl_1_r1_iso), .DATA_I(END), .RW(gpr_ctrl_1_r1_rw), .CLK(controlled_buffer_1_out), .RST(RST),
    .DATA_O(END), .SEN0(gpreg_8b_1_sen0), .SEN1(gpreg_8b_1_sen1));
  GPREG_8B gpreg_8b_2 (
    .ISO(gpr_ctrl_1_r0_iso), .DATA_I(END), .RW(gpr_ctrl_1_r0_rw), .CLK(controlled_buffer_1_out), .RST(RST),
    .DATA_O(END), .SEN0(R0), .SEN1(R1));
  Buffer_8B_NTS buffer_8b_nts_2 (.D(buffer_8b_nts_1_q), .T(or_4_out), .Q(END));
  or or_4 (or_4_out, eeprom_8kx16_1_out_2[6], not_4_out);
  not not_4 (not_4_out, eeprom_8kx16_1_out_2[11]);
  and and_6 (and_6_out, out_4[0], out_4[1], out_4[2], out_4[3], out_4[4], out_4[5]);
  not not_5 (not_5_out, out_4[6]);
  nor nor_2 (nor_2_out, _8, _14, _15);
  and and_7 (JMP, nor_2_out, _10);
  and and_8 (and_8_out, and_6_out, not_5_out);
  and and_9 (and_9_out, _10, not_6_out, _14);
  not not_6 (not_6_out, _8);
  not not_7 (not_7_out, _15);
  OFFSET_ADDER offset_adder_1 (.D(END), .CMD(_8), .GP(_10), .F1(_15), .F0(_14), .ADR(SPB[15:8]));
  _74374_8B_Reg_TS u_74374_8b_reg_ts_1 (
    .D(END), .CLK(controlled_buffer_1_out), .minus_OE(1'b0), .Q(SPB[7:0]), .RST(RST));
  Buffer_8B_NTS buffer_8b_nts_3 (.D(AD), .T(not_8_out), .Q(buffer_8b_nts_3_q));
  not not_8 (not_8_out, FT);
  nor nor_3 (eeprom_8kx16_1_out[6], FT, and_8_out);
  not not_9 (not_9_out, and_10_out);
  and and_10 (and_10_out, and_9_out, not_7_out);
  ProgramCounter__16B programcounter__16b_1 (
    .D(SPB), .HALT(nor_5_out), .CNT_LD(eeprom_8kx16_1_out_2[12]), .CLK(controlled_buffer_1_out), .RST(RST),
    .JmpToAdr(eeprom_8kx16_1_out_2[13]), .Q(SPBO), .ISO(PCI), .OL(OL), .OH(OH));  // open: RCO
  REG_8B_RW reg_8b_rw_1 (
    .WRT(1'b1), .Q(buffer_8b_nts_3_q), .READ(1'b1), .CLK(controlled_buffer_1_out), .RST(RST), .Q_2(out_4));
  and and_11 (FT, nor_4_out, out_4[6]);
  nor nor_4 (nor_4_out, out_4[5], out_4[4], out_4[3], out_4[2], out_4[1], out_4[0]);
  not not_10 (not_10_out, controlled_buffer_1_out);
  nand nand_1 (nand_1_out, and_10_out, and_9_out);
  not not_11 (not_11_out, not_9_out);
  Register #(.width(1)) register_1 (
    .D(not_9_out), .en(1'b1), .Q(register_1_q), .clk(controlled_buffer_1_out), .clr(1'b0));
  Hex_Digit_Display hex_digit_display_1 (.value(gpreg_8b_1_sen1));  // open: dp
  and and_12 (and_12_out, JMP, _7);
  nor nor_5 (nor_5_out, and_12_out, and_16_out, eeprom_8kx16_1_out_2[12]);
  EEPROM_8kX16 eeprom_8kx16_1 (
    .ADR({{5{1'b0}}, out_4}), .minus_CS(1'b1), .minus_OE(1'b0),
    .OUT({_15, _14, eeprom_8kx16_1_out_2[13:11], _10, eeprom_8kx16_1_out_2[9], _8, eeprom_8kx16_1_out_2[7:6], eeprom_8kx16_1_out[0], eeprom_8kx16_1_out[1], eeprom_8kx16_1_out[2], eeprom_8kx16_1_out[3], eeprom_8kx16_1_out[4], eeprom_8kx16_1_out[5]}));
  buf buffer_1 (buffer_1_out, FT);
  Buffer_8B_NTS buffer_8b_nts_4 (.D({1'b0, eeprom_8kx16_1_out}), .T(buffer_1_out), .Q(buffer_8b_nts_3_q));
  not not_12 (not_12_out, RST);
  or or_5 (or_5_out, not_10_out, nand_1_out);
  nand nand_2 (nand_2_out, and_9_out, not_9_out);
  and and_13 (and_13_out, not_11_out, register_1_q);
  and and_14 (and_14_out, and_9_out, not_9_out, not_13_out);
  not not_13 (not_13_out, register_1_q);
  not not_14 (not_14_out, and_9_out);
  and and_15 (and_15_out, not_9_out, not_14_out, register_1_q);
  Hex_Digit_Display hex_digit_display_2 (.value(gpreg_8b_1_sen0));  // open: dp
  Hex_Digit_Display hex_digit_display_3 (.value(R1));  // open: dp
  Register #(.width(1)) register_2 (
    .D(or_7_out), .en(1'b1), .Q(register_2_q), .clk(controlled_buffer_1_out), .clr(1'b0));
  Buffer_16B_NTS buffer_16b_nts_1 (.D(SPB), .T(RST), .Q(buffer_16b_nts_1_q));
  not not_15 (PCI, or_6_out);
  or or_6 (or_6_out, and_13_out, and_14_out, and_15_out);
  Hex_Digit_Display hex_digit_display_4 (.value(R0));  // open: dp
  or or_7 (or_7_out, and_17_out, and_18_out, and_19_out);
  and and_16 (and_16_out, register_2_q, JMP);
  nor nor_6 (nor_6_out, out_4[2], out_4[3], out_4[6], out_4[5]);
  StackRegister_16B stackregister_16b_1 (
    .D(buffer_16b_nts_1_q), .DOWN(or_5_out), .UP(nand_2_out), .LD(not_12_out), .RST(1'b0), .ISO(or_6_out),
    .Q(SPBO), .S(out_6), .CLK(controlled_buffer_1_out));  // open: OF, ZERO
  Pull_Resistor #(.pull(1)) pull_resistor_3 (.node({buffer_16b_nts_1_q[14], buffer_16b_nts_1_q[11]}));
  Pull_Resistor pull_resistor_4 (.node({buffer_16b_nts_1_q[15], buffer_16b_nts_1_q[13:12], buffer_16b_nts_1_q[10:0]}));
  xor xor_2 (xor_2_out, _6, FF[1]);
  xor xor_3 (xor_3_out, _6, FF[3]);
  and and_17 (and_17_out, xor_3_out, _14, not_17_out);
  and and_18 (and_18_out, xor_2_out, not_16_out, _15);
  and and_19 (and_19_out, xor_4_out, not_16_out, not_17_out);
  and and_20 (and_20_out, nor_6_out, out_4[4]);
  or or_8 (or_8_out, and_22_out, nor_7_out);
  xor xor_4 (xor_4_out, _6, FF[0]);
  Hex_Digit_Display hex_digit_display_5 (.value(mc_alu_8b_1_sen_b1));  // open: dp
  not not_16 (not_16_out, _14);
  not not_17 (not_17_out, _15);
  Hex_Digit_Display hex_digit_display_6 (.value(mc_alu_8b_1_sen_acc1));  // open: dp
  REGISTER_FLAG register_flag_1 (
    .IN(mc_alu_8b_1_flag), .WRT(register_3_q), .CLK(controlled_buffer_1_out), .RST(RST), .OUT(FF));
  not not_18 (not_18_out, and_20_out);
  Register #(.width(1)) register_3 (
    .D(nor_7_out), .en(1'b1), .Q(register_3_q), .clk(controlled_buffer_1_out), .clr(RST));
  nor nor_7 (nor_7_out, out_4[4], out_4[5], out_4[6]);
  Pull_Resistor #(.pull(1)) pull_resistor_5 (.node(pull_resistor_6_node[5]));
  Pull_Resistor pull_resistor_6 (.node({pull_resistor_6_node[15:6], pull_resistor_6_node[4:0]}));
  Hex_Digit_Display hex_digit_display_7 (.value(mc_alu_8b_1_sen_b0));  // open: dp
  Hex_Digit_Display hex_digit_display_8 (.value(mc_alu_8b_1_sen_acc0));  // open: dp
  MC_ALU_8B mc_alu_8b_1 (
    .DAT(END), .A_ISO(eeprom_8kx16_1_out_2[7]), .A_RW(eeprom_8kx16_1_out_2[9]), .SWP(and_20_out),
    .B_RW(not_18_out), .Start(or_8_out), .CMD_ISO(1'b1), .CMD_RW(_8), .CLK(controlled_buffer_1_out),
    .RST(RST), .Flag(mc_alu_8b_1_flag), .CMD_In(END), .CMD_Out(END), .DAT_O(END),
    .SEN_ACC1(mc_alu_8b_1_sen_acc1), .SEN_ACC0(mc_alu_8b_1_sen_acc0), .SEN_B1(mc_alu_8b_1_sen_b1),
    .SEN_B0(mc_alu_8b_1_sen_b0));  // open: Done, Z
  nor nor_8 (nor_8_out, out_4[0], out_4[2]);
  and and_21 (and_21_out, out_4[3], out_4[4], out_4[5]);
  and and_22 (and_22_out, and_21_out, out_4[2], out_4[6]);
  and and_23 (and_23_out, nor_8_out, out_4[1], and_21_out);
  not not_19 (not_19_out, out_4[6]);
  nand nand_3 (nand_3_out, and_23_out, out_4[6]);
  nand nand_4 (nand_4_out, and_23_out, not_19_out);
  assign AD = {undriven, END[5:0]};  // Buffer buffer_2, 8 bits wide
  Pull_Resistor pull_resistor_7 (.node(AD));
  Buffer_8B_NTS buffer_8b_nts_5 (.D(OL), .T(nand_3_out), .Q(END));
  Buffer_8B_NTS buffer_8b_nts_6 (.D(OH), .T(nand_4_out), .Q(END));

  // Other names for the same wires on the sheet: T[7:0] = END

  // Notes on the sheet:
  //   Bit 7
  //   2 Cycles to Init
  //   Bit 6
  //   GP1
  //   GP0
  //   PUSH/POP
  //   FTCH
  //   GPREG1
  //   NxtAdr
  //   GPREG0
  //   LD
  //   EQ C Z
  //   B
  //   Accumulator
endmodule

module _73163_4B_Counter (
  input  Down,
  input  [3:0] D,
  input  minus_LD,
  input  CLK,
  input  RST,
  output [3:0] Q,
  output RCO
);

  Counter #(.width(4), .max('hf)) counter_1 (
    .load(Down), .D(D), .count(minus_LD), .Q(Q), .carry(RCO), .clk(CLK), .clr(RST));

  // Notes on the sheet:
  //   Down must be 1 to load
endmodule

module ProgramCounter__16B (
  input  [15:0] D,
  input  HALT,
  input  CNT_LD,
  input  CLK,
  input  RST,
  input  JmpToAdr,
  input  ISO,
  output [15:0] Q,
  output [7:0] OL,
  output [7:0] OH,
  output RCO
);

  wire and_1_out, and_2_out, and_3_out, and_4_out, and_5_out, buffer_1_out, n73163_4b_counter_1_rco,
       n73163_4b_counter_2_rco, n73163_4b_counter_3_rco, n73163_4b_counter_4_rco, not_1_out, not_2_out,
       not_3_out, or_1_out, or_2_out;
  wire [15:0] register_1_q;

  not not_1 (not_1_out, HALT);
  and and_1 (and_1_out, not_1_out, not_2_out);
  not not_2 (not_2_out, CNT_LD);
  and and_2 (and_2_out, not_1_out, CNT_LD);
  Register #(.width(16)) register_1 (.D(D), .en(1'b1), .Q(register_1_q), .clk(CLK), .clr(RST));
  and and_3 (and_3_out, n73163_4b_counter_4_rco, and_2_out, n73163_4b_counter_3_rco, n73163_4b_counter_2_rco);
  and and_4 (and_4_out, and_2_out, n73163_4b_counter_4_rco, n73163_4b_counter_3_rco);
  and and_5 (and_5_out, and_2_out, n73163_4b_counter_4_rco);
  _73163_4B_Counter u_73163_4b_counter_1 (
    .Down(and_1_out), .D(D[15:12]), .minus_LD(and_3_out), .CLK(CLK), .RST(RST), .Q(OH[7:4]),
    .RCO(n73163_4b_counter_1_rco));
  _73163_4B_Counter u_73163_4b_counter_2 (
    .Down(and_1_out), .D(D[11:8]), .minus_LD(and_4_out), .CLK(CLK), .RST(RST), .Q(OH[3:0]),
    .RCO(n73163_4b_counter_2_rco));
  _73163_4B_Counter u_73163_4b_counter_3 (
    .Down(and_1_out), .D(D[7:4]), .minus_LD(and_5_out), .CLK(CLK), .RST(RST), .Q(OL[7:4]),
    .RCO(n73163_4b_counter_3_rco));
  _73163_4B_Counter u_73163_4b_counter_4 (
    .Down(and_1_out), .D(D[3:0]), .minus_LD(and_2_out), .CLK(CLK), .RST(RST), .Q(OL[3:0]),
    .RCO(n73163_4b_counter_4_rco));
  or or_1 (or_1_out, not_3_out, ISO);
  not not_3 (not_3_out, JmpToAdr);
  and and_6 (RCO, n73163_4b_counter_1_rco, n73163_4b_counter_2_rco, n73163_4b_counter_3_rco, n73163_4b_counter_4_rco);
  Buffer_8B_NTS buffer_8b_nts_1 (.D(register_1_q[7:0]), .T(or_1_out), .Q(Q[7:0]));
  Buffer_8B_NTS buffer_8b_nts_2 (.D(register_1_q[15:8]), .T(or_1_out), .Q(Q[15:8]));
  Buffer_8B_NTS buffer_8b_nts_3 (.D(OL), .T(or_2_out), .Q(Q[7:0]));
  Buffer_8B_NTS buffer_8b_nts_4 (.D(OH), .T(or_2_out), .Q(Q[15:8]));
  or or_2 (or_2_out, buffer_1_out, ISO);
  buf buffer_1 (buffer_1_out, JmpToAdr);

  // Notes on the sheet:
  //   1=CNT
  //   3
  //   2
  //   1
  //   0
endmodule

module AT28C64B_EEPROM_8kx8_Channel_A (
  input  [12:0] ADR,
  input  minus_CS,
  input  minus_OE,
  output [7:0] Out
);

  wire [7:0] rom_1_data;

  ROM #(.addrWidth(13)) rom_1 (.addr(ADR), .data(rom_1_data), .sel(minus_CS));
  Buffer_8B_NTS buffer_8b_nts_1 (.D(rom_1_data), .T(minus_OE), .Q(Out));

  // Notes on the sheet:
  //   contents of rom_1 (hex, n*v repeats v):
  //   16*cb c9 c9 cb cb 88 cb cb 88 4a db db 4*8a 18 5a db db 4*8a db 9b 1b 5b cb cb c9 cb cb cb db cb c9
  //   6*cb c6 4e c6 4e cb cb da cb cb cb c9 e e cb f3 cb b2 db e cb 4e e c9 db db 88 ca ca cb 4a db 4*0 88
  //   cb cb 4a cb f9 cb 7a f e9 cf e9 f e3 cf e3 f 6f cf 6f f a7 cf a7 db 4*0 c6 0 db db
endmodule

module EEPROM_8kX16 (
  input  [12:0] ADR,
  input  minus_CS,
  input  minus_OE,
  output [15:0] OUT
);

  AT28C64B_EEPROM_8kx8_Channel_A at28c64b_eeprom_8kx8_channel_a_1 (
    .ADR(ADR), .minus_CS(minus_CS), .minus_OE(minus_OE), .Out(OUT[15:8]));
  AT28C64B_EEPROM_8kx8_Channel_B at28c64b_eeprom_8kx8_channel_b_1 (
    .ADR(ADR), .minus_CS(minus_CS), .minus_OE(minus_OE), .Out(OUT[7:0]));

  // Notes on the sheet:
  //   PROM_1
  //   PROM_0
endmodule

module AT28C64B_EEPROM_8kx8_Channel_B (
  input  [12:0] ADR,
  input  minus_CS,
  input  minus_OE,
  output [7:0] Out
);

  wire [7:0] rom_1_data;

  ROM #(.addrWidth(13)) rom_1 (.addr(ADR), .data(rom_1_data), .sel(minus_CS));
  Buffer_8B_NTS buffer_8b_nts_1 (.D(rom_1_data), .T(minus_OE), .Q(Out));

  // Notes on the sheet:
  //   contents of rom_1 (hex, n*v repeats v):
  //   14*f0 c0 c0 40 72 c0 c0 ea c0 c0 c0 40 a1 b1 e9 ed f9 fd 80 80 b8 a4 e5 e3 f5 f3 98 a8 a8 a8 c0 40
  //   c0 c0 c0 40 ab 40 40 6*c0 ac dc 0 c2 c0 ff 80 c0 c0 c0 40 86 80 84 0 94 80 8c 80 d7 bc a2 80 d2 c0
  //   ca 8f af fa 40 c0 4*0 de fe 81 48 91 0 89 80 99 80 85 80 95 0 8d 0 9d 80 83 80 93 80 8b 80 80 4*0 b4
  //   0 f0 da
endmodule

module GPREG_8B (
  input  ISO,
  input  [7:0] DATA_I,
  input  RW,
  input  CLK,
  input  RST,
  output [7:0] DATA_O,
  output [3:0] SEN0,
  output [3:0] SEN1
);

  wire nand_1_out, not_1_out;
  wire [7:0] buffer_8b_nts_2_q;

  nand nand_1 (nand_1_out, ISO, RW);
  Buffer_8B_NTS buffer_8b_nts_1 (.D(buffer_8b_nts_2_q), .T(nand_1_out), .Q(DATA_O));
  not not_1 (not_1_out, RW);
  Buffer_8B_NTS buffer_8b_nts_2 (.D({SEN1, SEN0}), .T(not_1_out), .Q(buffer_8b_nts_2_q));
  Buffer_8B_NTS buffer_8b_nts_3 (.D(DATA_I), .T(RW), .Q(buffer_8b_nts_2_q));
  Register register_1 (.D(buffer_8b_nts_2_q), .en(1'b1), .Q({SEN1, SEN0}), .clk(CLK), .clr(RST));

  // Notes on the sheet:
  //   1=R
  //   0=ISO
endmodule

module GPR_CTRL (
  input  ENA,
  input  B6,
  input  F1,
  input  F0,
  output R0_ISO,
  output R0_RW,
  output R1_ISO,
  output R1_RW
);

  wire and_1_out, and_2_out, and_3_out, and_4_out, and_5_out, and_6_out, not_1_out, not_2_out, not_3_out,
       not_4_out;

  not not_1 (not_1_out, ENA);
  not not_2 (not_2_out, B6);
  not not_3 (not_3_out, F0);
  not not_4 (not_4_out, F1);
  and and_1 (and_1_out, F0, not_4_out, ENA, not_2_out);
  and and_2 (and_2_out, not_3_out, F1, ENA, not_2_out);
  and and_3 (and_3_out, not_2_out, not_4_out);
  and and_4 (and_4_out, not_3_out, F1, ENA, B6);
  and and_5 (and_5_out, F0, not_4_out, ENA, B6);
  and and_6 (and_6_out, B6, not_4_out);
  or or_1 (R0_ISO, and_1_out, and_2_out);
  or or_2 (R0_RW, and_3_out, B6, F0, not_1_out);
  or or_3 (R1_ISO, and_4_out, and_5_out);
  or or_4 (R1_RW, and_6_out, not_2_out, F0, not_1_out);
endmodule

module REGISTER_FLAG (
  input  [3:0] IN,
  input  WRT,
  input  CLK,
  input  RST,
  output [3:0] OUT
);

  wire [3:0] multiplexer_1_out;

  Multiplexer #(.width(4), .enable("false")) multiplexer_1 (.in0(OUT), .in1(IN), .out(multiplexer_1_out), .sel(WRT));
  Register #(.width(4)) register_1 (.D(multiplexer_1_out), .en(1'b1), .Q(OUT), .clk(CLK), .clr(RST));
endmodule

module REGPUSH_4B (
  input  D,
  input  CLK,
  input  RST,
  output Q0,
  output Q1,
  output Q2,
  output Q3
);

  Register #(.width(1)) register_1 (.D(D), .en(1'b1), .Q(Q0), .clk(CLK), .clr(RST));
  Register #(.width(1)) register_2 (.D(Q0), .en(1'b1), .Q(Q1), .clk(CLK), .clr(RST));
  Register #(.width(1)) register_3 (.D(Q1), .en(1'b1), .Q(Q2), .clk(CLK), .clr(RST));
  Register #(.width(1)) register_4 (.D(Q2), .en(1'b1), .Q(Q3), .clk(CLK), .clr(RST));
endmodule

module StackRegister_16B (
  input  [15:0] D,
  input  CLK,
  input  DOWN,
  input  UP,
  input  LD,
  input  RST,
  input  ISO,
  output [15:0] S,
  output [15:0] Q,
  output OF,
  output ZERO
);

  wire and_1_out, n74ls193_2_b, n74ls193_2_c, n74ls193_3_b, n74ls193_3_c, n74ls193_4_c, nor_1_out, not_1_out,
       not_2_out, or_1_out, register_1_q, register_2_q;

  not not_1 (not_1_out, CLK);
  and and_1 (and_1_out, not_1_out, CLK);
  not not_2 (not_2_out, CLK);
  nor nor_1 (nor_1_out, not_2_out, CLK);
  Register #(.width(1)) register_1 (.D(UP), .en(1'b1), .Q(register_1_q), .clk(or_1_out), .clr(1'b0));
  or or_1 (or_1_out, and_1_out, nor_1_out);
  Register #(.width(1)) register_2 (.D(DOWN), .en(1'b1), .Q(register_2_q), .clk(or_1_out), .clr(1'b0));
  _74LS193 u_74ls193_1 (
    .D0(D[12]), .D1(D[13]), .D2(D[14]), .D3(D[15]), .LD(LD), .UP(n74ls193_2_c), .DWN(n74ls193_2_b),
    .CLR(RST), .C(OF), .Q0(S[12]), .Q1(S[13]), .Q2(S[14]), .Q3(S[15]));  // open: B
  _74LS193 u_74ls193_2 (
    .D0(D[8]), .D1(D[9]), .D2(D[10]), .D3(D[11]), .LD(LD), .UP(n74ls193_3_c), .DWN(n74ls193_3_b), .CLR(RST),
    .C(n74ls193_2_c), .B(n74ls193_2_b), .Q0(S[8]), .Q1(S[9]), .Q2(S[10]), .Q3(S[11]));
  _74LS193 u_74ls193_3 (
    .D0(D[4]), .D1(D[5]), .D2(D[6]), .D3(D[7]), .LD(LD), .UP(n74ls193_4_c), .DWN(ZERO), .CLR(RST),
    .C(n74ls193_3_c), .B(n74ls193_3_b), .Q0(S[4]), .Q1(S[5]), .Q2(S[6]), .Q3(S[7]));
  _74LS193 u_74ls193_4 (
    .D0(D[0]), .D1(D[1]), .D2(D[2]), .D3(D[3]), .LD(LD), .UP(register_1_q), .DWN(register_2_q), .CLR(RST),
    .C(n74ls193_4_c), .B(ZERO), .Q0(S[0]), .Q1(S[1]), .Q2(S[2]), .Q3(S[3]));
  Buffer_8B_NTS buffer_8b_nts_1 (.D(S[7:0]), .T(ISO), .Q(Q[7:0]));
  Buffer_8B_NTS buffer_8b_nts_2 (.D(S[15:8]), .T(ISO), .Q(Q[15:8]));
endmodule

module _74LS193 (
  input  D0,
  input  D1,
  input  D2,
  input  D3,
  input  LD,
  input  UP,
  input  DWN,
  input  CLR,
  output C,
  output B,
  output Q0,
  output Q1,
  output Q2,
  output Q3
);

  wire and_1_out, and_2_out, and_3_out, and_4_out, and_5_out, and_6_out, buffer_1_out, buffer_2_out,
       buffer_3_out, buffer_5_out, buffer_7_out, buffer_9_out, nand_1_out, nand_2_out, nand_3_out,
       nand_4_out, nand_5_out, nand_6_out, nand_7_out, nand_8_out, nand_9_out, nand_10_out, nor_1_out,
       nor_2_out, nor_3_out, nor_4_out, not_1_out, not_2_out, not_3_out, not_4_out, not_5_out, not_6_out,
       not_7_out, not_8_out, or_1_out, or_2_out, or_3_out, or_4_out, t_ff_1_q, t_ff_1_qn, t_ff_2_q,
       t_ff_2_qn, t_ff_3_q, t_ff_3_qn, t_ff_4_q, t_ff_4_qn;

  not not_1 (not_1_out, LD);
  not not_2 (not_2_out, UP);
  buf buffer_1 (buffer_1_out, not_2_out);
  buf buffer_2 (buffer_2_out, not_3_out);
  not not_3 (not_3_out, DWN);
  not not_4 (not_4_out, CLR);
  buf buffer_3 (buffer_3_out, D0);
  nand nand_1 (nand_1_out, not_1_out, buffer_3_out);
  not not_5 (not_5_out, nand_1_out);
  nor nor_1 (nor_1_out, buffer_1_out, buffer_2_out);
  nand nand_2 (nand_2_out, nand_1_out, not_1_out);
  T_Flip_Flop t_ff_1 (
    .clk(nor_1_out), .T(nor_1_out), .Q(t_ff_1_q), .Qn(t_ff_1_qn), .preset(not_5_out), .reset(or_1_out));  // open: en
  or or_1 (or_1_out, ~not_4_out, ~nand_2_out);  // OR_Gate
  buf buffer_4 (Q0, t_ff_1_q);
  and and_1 (and_1_out, not_2_out, t_ff_1_q);
  nor nor_2 (nor_2_out, and_1_out, and_2_out);
  and and_2 (and_2_out, t_ff_1_qn, not_3_out);
  buf buffer_5 (buffer_5_out, D1);
  nand nand_3 (nand_3_out, not_1_out, buffer_5_out);
  nand nand_4 (nand_4_out, nand_3_out, not_1_out);
  not not_6 (not_6_out, nand_3_out);
  T_Flip_Flop t_ff_2 (
    .clk(nor_2_out), .T(nor_2_out), .Q(t_ff_2_q), .Qn(t_ff_2_qn), .preset(not_6_out), .reset(or_2_out));  // open: en
  or or_2 (or_2_out, ~not_4_out, ~nand_4_out);  // OR_Gate
  buf buffer_6 (Q1, t_ff_2_q);
  and and_3 (and_3_out, not_2_out, t_ff_1_q, t_ff_2_q);
  nor nor_3 (nor_3_out, and_3_out, and_4_out);
  and and_4 (and_4_out, t_ff_2_qn, t_ff_1_qn, not_3_out);
  buf buffer_7 (buffer_7_out, D2);
  nand nand_5 (nand_5_out, not_1_out, buffer_7_out);
  nand nand_6 (nand_6_out, nand_5_out, not_1_out);
  not not_7 (not_7_out, nand_5_out);
  T_Flip_Flop t_ff_3 (
    .clk(nor_3_out), .T(nor_3_out), .Q(t_ff_3_q), .Qn(t_ff_3_qn), .preset(not_7_out), .reset(or_3_out));  // open: en
  or or_3 (or_3_out, ~not_4_out, ~nand_6_out);  // OR_Gate
  buf buffer_8 (Q2, t_ff_3_q);
  and and_5 (and_5_out, t_ff_2_q, not_2_out, t_ff_1_q, t_ff_3_q);
  nor nor_4 (nor_4_out, and_5_out, and_6_out);
  and and_6 (and_6_out, t_ff_3_qn, t_ff_2_qn, t_ff_1_qn, not_3_out);
  buf buffer_9 (buffer_9_out, D3);
  nand nand_7 (nand_7_out, not_1_out, buffer_9_out);
  nand nand_8 (nand_8_out, nand_7_out, not_1_out);
  not not_8 (not_8_out, nand_7_out);
  T_Flip_Flop t_ff_4 (
    .clk(nor_4_out), .T(nor_4_out), .Q(t_ff_4_q), .Qn(t_ff_4_qn), .preset(not_8_out), .reset(or_4_out));  // open: en
  or or_4 (or_4_out, ~not_4_out, ~nand_8_out);  // OR_Gate
  nand nand_9 (nand_9_out, t_ff_3_q, not_2_out, t_ff_4_q, t_ff_2_q, t_ff_1_q);
  nand nand_10 (nand_10_out, t_ff_1_qn, t_ff_4_qn, t_ff_3_qn, t_ff_2_qn, not_3_out);
  buf buffer_10 (Q3, t_ff_4_q);
  buf buffer_11 (C, nand_9_out);
  buf buffer_12 (B, nand_10_out);
endmodule

module Buffer_16B_NTS (
  input  [15:0] D,
  input  T,
  output [15:0] Q
);

  wire not_1_out;

  assign Q = not_1_out ? D : 16'bz;  // Controlled_Buffer controlled_buffer_1
  not not_1 (not_1_out, T);
endmodule

module OFFSET_ADDER (
  input  [7:0] D,
  input  CMD,
  input  GP,
  input  F1,
  input  F0,
  output [7:0] ADR
);

  wire and_1_out, not_1_out, not_2_out;
  wire [1:0] and_3_out;

  and and_1 (and_1_out, CMD, GP);
  not not_1 (not_1_out, F1);
  not not_2 (not_2_out, F0);
  and and_2 (and_3_out[1], and_1_out, F0, F1);
  and and_3 (and_3_out[0], and_1_out, not_1_out, not_2_out);
  Multiplexer #(.select(2), .width(8), .enable("false")) multiplexer_1 (
    .in0(D), .in1(8'h48), .in2(8'h58), .in3({8{1'b1}}), .out(ADR), .sel(and_3_out));
endmodule

module CU_8B (
  input  [7:0] in_1,
  input  [7:0] in_2,
  input  INT1,
  input  INT0,
  output [7:0] STATE
);

  wire and_1_out, and_2_out, and_3_out, and_4_out, and_5_out, and_6_out, and_7_out, and_8_out, and_9_out,
       and_10_out, and_11_out, and_12_out, and_13_out, and_14_out, and_15_out, and_16_out, and_17_out,
       and_18_out, and_19_out, and_20_out, and_21_out, and_22_out, and_23_out, and_24_out, and_25_out,
       and_26_out, and_27_out, and_28_out, and_29_out, and_30_out, and_31_out, and_32_out, and_33_out,
       and_34_out, and_35_out, and_36_out, buffer_2_out, CLK_out, demultiplexer_1_out0, demultiplexer_1_out1,
       gpr_ctrl_1_r0_iso, gpr_ctrl_1_r0_rw, gpr_ctrl_1_r1_iso, gpr_ctrl_1_r1_rw, multiplexer_1_out,
       nand_1_out, nand_2_out, nand_3_out, nand_4_out, nand_5_out, nand_6_out, nand_7_out, nand_8_out,
       nand_9_out, nand_10_out, nand_11_out, nand_12_out, nand_13_out, nand_14_out, nand_15_out, nand_16_out,
       nand_17_out, nand_18_out, nand_19_out, nand_20_out, nand_21_out, nand_22_out, nand_23_out,
       nand_24_out, nand_25_out, nand_26_out, nand_27_out, nand_28_out, nand_29_out, nand_30_out,
       nand_31_out, nor_1_out, nor_3_out, nor_4_out, nor_5_out, nor_6_out, nor_7_out, nor_8_out, not_1_out,
       not_2_out, not_3_out, not_4_out, not_5_out, not_6_out, not_7_out, not_8_out, not_9_out, not_10_out,
       not_11_out, not_12_out, not_13_out, not_14_out, not_15_out, not_16_out, not_17_out, not_18_out,
       not_19_out, not_20_out, not_21_out, not_22_out, not_23_out, not_24_out, not_25_out, not_26_out,
       not_27_out, not_28_out, not_29_out, or_1_out, or_2_out, or_3_out, or_4_out, or_5_out, or_6_out,
       or_7_out, or_8_out, or_9_out, register_1_q, register_2_q, register_3_q, register_4_q, register_5_q,
       register_6_q, register_7_q, register_8_q, register_9_q, regpush_4b_1_q0, regpush_4b_1_q1,
       regpush_4b_1_q2, regpush_4b_2_q0, regpush_4b_2_q1, regpush_4b_2_q2, RES_out, RST_out, xnor_1_out,
       xor_1_out, xor_2_out, xor_3_out, xor_4_out, xor_5_out;
  wire [3:0] A0, A1, B0, B1, G00, G01, G10, G11, GP0, GP1, GP2, GP3, mc_alu_8b_1_flag, PC0, PC1, PC2, PC3,
       register_flag_1_out, SP0, SP1, SP2, SP3;
  wire [6:0] eeprom_8kx16_1_out;
  wire [7:0] buffer_8b_nts_1_q, buffer_8b_nts_2_q, controlled_buffer_1_out, controlled_buffer_7_out,
       port_ext_1_odat_o, port_ext_2_odat_o, programcounter__16b_1_oh, programcounter__16b_1_ol,
       pull_resistor_7_node;
  wire [7:6] undriven;
  wire [15:0] buffer_16b_nts_1_q, multiplexer_2_out, n74374_8b_reg_ts_1_q;
  wire [15:6] eeprom_8kx16_1_out_2;

  Button RES (.out(RES_out));
  Button CLK (.out(CLK_out));
  Hex_Digit_Display hex_digit_display_1 (.value(A1));  // open: dp
  Pull_Resistor pull_resistor_1 (.node(INT1));
  Pull_Resistor pull_resistor_2 (.node(INT0));
  Hex_Digit_Display hex_digit_display_2 (.value(A0));  // open: dp
  and and_1 (and_1_out, buffer_8b_nts_2_q[6], not_22_out);
  Pull_Resistor pull_resistor_3 (.node(and_1_out));
  and and_2 (and_2_out, buffer_8b_nts_2_q[7], not_22_out);
  Pull_Resistor pull_resistor_4 (.node(and_2_out));
  nand nand_1 (nand_1_out, nand_2_out, not_1_out);
  Register #(.width(1)) register_1 (.D(or_1_out), .en(1'b1), .Q(register_1_q), .clk(CLK_out), .clr(or_3_out));
  or or_1 (or_1_out, register_1_q, INT1);
  or or_2 (or_2_out, register_2_q, INT0);
  Register #(.width(1)) register_2 (.D(or_2_out), .en(1'b1), .Q(register_2_q), .clk(CLK_out), .clr(or_3_out));
  or or_3 (or_3_out, and_3_out, RES_out);
  and and_3 (and_3_out, register_7_q, register_6_q);
  Hex_Digit_Display hex_digit_display_3 (.value(B1));  // open: dp
  REGPUSH_4B regpush_4b_1 (
    .D(and_1_out), .CLK(CLK_out), .RST(nand_1_out), .Q0(regpush_4b_1_q0), .Q1(regpush_4b_1_q1),
    .Q2(regpush_4b_1_q2));  // open: Q3
  or or_4 (or_4_out, regpush_4b_1_q0, regpush_4b_1_q1, regpush_4b_1_q2);
  REGPUSH_4B regpush_4b_2 (
    .D(and_2_out), .CLK(CLK_out), .RST(nand_1_out), .Q0(regpush_4b_2_q0), .Q1(regpush_4b_2_q1),
    .Q2(regpush_4b_2_q2));  // open: Q3
  or or_5 (or_5_out, regpush_4b_2_q0, regpush_4b_2_q1, regpush_4b_2_q2);
  nand nand_2 (nand_2_out, nor_1_out, not_22_out);
  not not_1 (not_1_out, RES_out);
  not not_2 (not_2_out, or_7_out);
  not not_3 (not_3_out, eeprom_8kx16_1_out_2[8]);
  and and_4 (and_4_out, not_3_out, eeprom_8kx16_1_out_2[14], eeprom_8kx16_1_out_2[10]);
  not not_4 (not_4_out, eeprom_8kx16_1_out_2[15]);
  or or_6 (or_6_out, register_1_q, register_2_q);
  or or_7 (or_7_out, register_7_q, register_6_q);
  and and_5 (and_5_out, eeprom_8kx16_1_out_2[12], or_7_out);
  or or_8 (or_8_out, and_5_out, nand_20_out, register_5_q);
  Hex_Digit_Display hex_digit_display_4 (.value(B0));  // open: dp
  Multiplexer #(.enable("false")) multiplexer_1 (
    .in0(or_4_out), .in1(or_5_out), .out(multiplexer_1_out), .sel(and_6_out));
  and and_6 (and_6_out, eeprom_8kx16_1_out_2[10], eeprom_8kx16_1_out_2[8]);
  not not_5 (not_5_out, CLK_out);
  nor nor_1 (nor_1_out, not_5_out, CLK_out);
  Buffer_8B_NTS buffer_8b_nts_1 (.D(buffer_8b_nts_2_q), .T(eeprom_8kx16_1_out_2[11]), .Q(buffer_8b_nts_1_q));
  RAM #(.addrWidth(16)) ram_1 (
    .addr({PC3, PC2, PC1, PC0}), .data(buffer_8b_nts_1_q), .sel(not_9_out), .clk(CLK_out),
    .ld(eeprom_8kx16_1_out_2[11]), .clr(1'b0));
  nand nand_3 (nand_3_out, and_4_out, not_7_out);
  not not_6 (not_6_out, nand_3_out);
  not not_7 (not_7_out, nand_4_out);
  nand nand_4 (nand_4_out, and_4_out, not_4_out);
  Register #(.width(1)) register_3 (.D(nand_4_out), .en(1'b1), .Q(register_3_q), .clk(CLK_out), .clr(1'b0));
  and and_7 (and_7_out, and_13_out, or_6_out);
  Register #(.width(1)) register_4 (.D(or_8_out), .en(1'b1), .Q(register_4_q), .clk(CLK_out), .clr(RES_out));
  not not_8 (not_8_out, CLK_out);
  Hex_Digit_Display hex_digit_display_5 (.value(G10));  // open: dp
  Hex_Digit_Display hex_digit_display_6 (.value(G11));  // open: dp
  xnor xnor_1 (xnor_1_out, eeprom_8kx16_1_out_2[10], eeprom_8kx16_1_out_2[8]);
  and and_8 (and_8_out, xnor_1_out, xor_1_out);
  xor xor_1 (xor_1_out, eeprom_8kx16_1_out_2[15], eeprom_8kx16_1_out_2[14]);
  Buffer_8B_NTS buffer_8b_nts_2 (.D(buffer_8b_nts_1_q), .T(nand_5_out), .Q(buffer_8b_nts_2_q));
  nand nand_5 (nand_5_out, not_2_out, eeprom_8kx16_1_out_2[11], not_9_out);
  not not_9 (not_9_out, eeprom_8kx16_1_out_2[6]);
  not not_10 (not_10_out, RES_out);
  nand nand_6 (nand_6_out, CLK_out, not_6_out);
  not not_11 (not_11_out, nand_8_out);
  nand nand_7 (nand_7_out, and_4_out, nand_4_out);
  not not_12 (not_12_out, nand_4_out);
  not not_13 (not_13_out, register_3_q);
  not not_14 (not_14_out, and_4_out);
  Register #(.width(1)) register_5 (.D(and_7_out), .en(1'b1), .Q(register_5_q), .clk(CLK_out), .clr(RES_out));
  not not_15 (not_15_out, register_7_q);
  not not_16 (not_16_out, register_6_q);
  Register #(.width(1)) register_6 (.D(not_16_out), .en(1'b1), .Q(register_6_q), .clk(and_9_out), .clr(or_3_out));
  and and_9 (and_9_out, not_8_out, register_4_q);
  Hex_Digit_Display hex_digit_display_7 (.value(G01));  // open: dp
  GPR_CTRL gpr_ctrl_1 (
    .R0_ISO(gpr_ctrl_1_r0_iso), .R0_RW(gpr_ctrl_1_r0_rw), .R1_ISO(gpr_ctrl_1_r1_iso),
    .R1_RW(gpr_ctrl_1_r1_rw), .ENA(and_8_out), .B6(multiplexer_1_out), .F1(eeprom_8kx16_1_out_2[14]),
    .F0(eeprom_8kx16_1_out_2[15]));
  Buffer_16B_NTS buffer_16b_nts_1 (.D(n74374_8b_reg_ts_1_q), .T(RES_out), .Q(buffer_16b_nts_1_q));
  nand nand_8 (nand_8_out, nand_9_out, nand_10_out, nand_11_out);
  nand nand_9 (nand_9_out, not_12_out, register_3_q);
  nand nand_10 (nand_10_out, not_13_out, and_4_out, nand_4_out);
  nand nand_11 (nand_11_out, not_14_out, register_3_q, nand_4_out);
  not not_17 (not_17_out, register_6_q);
  and and_10 (and_10_out, not_15_out, and_18_out, register_6_q);
  Demultiplexer #(.enable("false")) demultiplexer_1 (
    .out0(demultiplexer_1_out0), .out1(demultiplexer_1_out1), .in(and_10_out), .sel(register_1_q));
  xor xor_2 (xor_2_out, register_7_q, register_6_q);
  Hex_Digit_Display hex_digit_display_8 (.value(G00));  // open: dp
  GPREG_8B gpreg_8b_1 (
    .ISO(gpr_ctrl_1_r0_iso), .DATA_I(buffer_8b_nts_2_q), .RW(gpr_ctrl_1_r0_rw), .CLK(CLK_out), .RST(RES_out),
    .DATA_O(buffer_8b_nts_2_q), .SEN0(G00), .SEN1(G01));
  GPREG_8B gpreg_8b_2 (
    .ISO(gpr_ctrl_1_r1_iso), .DATA_I(buffer_8b_nts_2_q), .RW(gpr_ctrl_1_r1_rw), .CLK(CLK_out), .RST(RES_out),
    .DATA_O(buffer_8b_nts_2_q), .SEN0(G10), .SEN1(G11));
  StackRegister_16B stackregister_16b_1 (
    .D(buffer_16b_nts_1_q), .DOWN(nand_6_out), .UP(nand_7_out), .LD(not_10_out), .RST(1'b0),
    .ISO(nand_8_out), .Q({PC3, PC2, PC1, PC0}), .S({SP3, SP2, SP1, SP0}), .CLK(CLK_out));  // open: OF, ZERO
  Pull_Resistor #(.pull(1)) pull_resistor_5 (.node({buffer_16b_nts_1_q[14], buffer_16b_nts_1_q[11]}));
  Pull_Resistor pull_resistor_6 (.node({buffer_16b_nts_1_q[15], buffer_16b_nts_1_q[13:12], buffer_16b_nts_1_q[10:0]}));
  assign controlled_buffer_1_out = and_7_out ? 8'h3a : 8'bz;  // Controlled_Buffer controlled_buffer_1
  assign buffer_8b_nts_2_q = and_11_out ? {8{1'b1}} : 8'bz;  // Controlled_Buffer controlled_buffer_2
  and and_11 (and_11_out, not_17_out, and_18_out, register_7_q);
  assign buffer_8b_nts_2_q = demultiplexer_1_out0 ? 8'hc0 : 8'bz;  // Controlled_Buffer controlled_buffer_3
  assign buffer_8b_nts_2_q = demultiplexer_1_out1 ? 8'he0 : 8'bz;  // Controlled_Buffer controlled_buffer_4
  Register #(.width(1)) register_7 (.D(xor_2_out), .en(1'b1), .Q(register_7_q), .clk(and_9_out), .clr(or_3_out));
  Hex_Digit_Display hex_digit_display_9 (.value(PC3));  // open: dp
  Hex_Digit_Display hex_digit_display_10 (.value(PC2));  // open: dp
  Pull_Resistor pull_resistor_7 (.node(pull_resistor_7_node));
  assign pull_resistor_7_node = {undriven, buffer_8b_nts_2_q[5:0]};  // Buffer buffer_1, 8 bits wide
  Hex_Digit_Display hex_digit_display_11 (.value(PC1));  // open: dp
  Buffer_8B_NTS buffer_8b_nts_3 (.D(pull_resistor_7_node), .T(not_18_out), .Q(controlled_buffer_1_out));
  not not_18 (not_18_out, not_22_out);
  nor nor_2 (eeprom_8kx16_1_out[6], not_22_out, and_14_out);
  and and_12 (and_12_out, STATE[3], STATE[4], STATE[5]);
  not not_19 (not_19_out, or_6_out);
  Hex_Digit_Display hex_digit_display_12 (.value(PC0));  // open: dp
  OFFSET_ADDER offset_adder_1 (
    .D(buffer_8b_nts_2_q), .CMD(eeprom_8kx16_1_out_2[8]), .GP(eeprom_8kx16_1_out_2[10]),
    .F1(eeprom_8kx16_1_out_2[14]), .F0(eeprom_8kx16_1_out_2[15]), .ADR(n74374_8b_reg_ts_1_q[15:8]));
  _74374_8B_Reg_TS u_74374_8b_reg_ts_1 (
    .D(buffer_8b_nts_2_q), .CLK(CLK_out), .minus_OE(1'b0), .Q(n74374_8b_reg_ts_1_q[7:0]), .RST(RES_out));
  REG_8B_RW reg_8b_rw_1 (
    .WRT(1'b1), .Q(controlled_buffer_1_out), .READ(1'b1), .CLK(CLK_out), .RST(RES_out), .Q_2(STATE));
  and and_13 (and_13_out, nor_3_out, buffer_2_out);
  buf buffer_2 (buffer_2_out, STATE[6]);
  nor nor_3 (nor_3_out, STATE[5], STATE[4], STATE[3], STATE[2], STATE[1], STATE[0]);
  not not_20 (not_20_out, STATE[6]);
  and and_14 (and_14_out, not_20_out, and_15_out);
  and and_15 (and_15_out, STATE[5], STATE[4], STATE[3], STATE[2], STATE[1], STATE[0]);
  nor nor_4 (nor_4_out, STATE[0], STATE[2]);
  and and_16 (and_16_out, nor_4_out, STATE[1], and_12_out);
  and and_17 (and_17_out, and_12_out, STATE[2], STATE[6]);
  nand nand_12 (nand_12_out, and_13_out, not_19_out);
  nand nand_13 (nand_13_out, and_13_out, or_6_out);
  Hex_Digit_Display hex_digit_display_13 (.value(SP2));  // open: dp
  Hex_Digit_Display hex_digit_display_14 (.value(SP3));  // open: dp
  Buffer_8B_NTS buffer_8b_nts_4 (.D({1'b0, eeprom_8kx16_1_out}), .T(nand_14_out), .Q(controlled_buffer_1_out));
  not not_21 (not_21_out, STATE[6]);
  and and_18 (and_18_out, nand_18_out, nand_17_out);
  not not_22 (not_22_out, nand_12_out);
  nand nand_14 (nand_14_out, nand_12_out, nand_13_out);
  Hex_Digit_Display hex_digit_display_15 (.value(SP1));  // open: dp
  ProgramCounter__16B programcounter__16b_1 (
    .D(n74374_8b_reg_ts_1_q), .HALT(nand_15_out), .CNT_LD(eeprom_8kx16_1_out_2[12]), .CLK(CLK_out),
    .RST(RES_out), .JmpToAdr(eeprom_8kx16_1_out_2[13]), .Q({PC3, PC2, PC1, PC0}), .ISO(not_11_out),
    .OL(programcounter__16b_1_ol), .OH(programcounter__16b_1_oh));  // open: RCO
  nand nand_15 (nand_15_out, nand_16_out, nand_16_out);
  nand nand_16 (nand_16_out, nand_19_out, nand_21_out);
  EEPROM_8kX16 eeprom_8kx16_1 (
    .ADR({{5{1'b0}}, STATE}), .minus_CS(1'b1), .minus_OE(1'b0),
    .OUT({eeprom_8kx16_1_out_2, eeprom_8kx16_1_out[0], eeprom_8kx16_1_out[1], eeprom_8kx16_1_out[2], eeprom_8kx16_1_out[3], eeprom_8kx16_1_out[4], eeprom_8kx16_1_out[5]}));
  Buffer_8B_NTS buffer_8b_nts_5 (.D(programcounter__16b_1_ol), .T(nand_17_out), .Q(buffer_8b_nts_2_q));
  nand nand_17 (nand_17_out, and_16_out, STATE[6]);
  Buffer_8B_NTS buffer_8b_nts_6 (.D(programcounter__16b_1_oh), .T(nand_18_out), .Q(buffer_8b_nts_2_q));
  nand nand_18 (nand_18_out, and_16_out, not_21_out);
  Hex_Digit_Display hex_digit_display_16 (.value(SP0));  // open: dp
  Register #(.width(1)) register_8 (.D(nand_22_out), .en(1'b1), .Q(register_8_q), .clk(CLK_out), .clr(1'b0));
  nand nand_19 (nand_19_out, nand_24_out, nand_20_out);
  nand nand_20 (nand_20_out, nand_25_out, nand_25_out);
  nand nand_21 (nand_21_out, eeprom_8kx16_1_out_2[12], eeprom_8kx16_1_out_2[12]);
  Hex_Digit_Display hex_digit_display_17 (.value(GP3));  // open: dp
  Hex_Digit_Display hex_digit_display_18 (.value(GP2));  // open: dp
  nand nand_22 (nand_22_out, nand_26_out, nand_27_out, nand_28_out);
  nand nand_23 (nand_23_out, register_8_q, register_8_q);
  nand nand_24 (nand_24_out, nand_23_out, or_5_out);
  nand nand_25 (nand_25_out, nand_31_out, nand_30_out, eeprom_8kx16_1_out_2[10], nand_29_out);
  Hex_Digit_Display hex_digit_display_19 (.value(GP1));  // open: dp
  Hex_Digit_Display hex_digit_display_20 (.value(GP0));  // open: dp
  nand nand_26 (nand_26_out, xor_5_out, eeprom_8kx16_1_out_2[14], nand_30_out);
  nand nand_27 (nand_27_out, nand_31_out, xor_4_out, eeprom_8kx16_1_out_2[15]);
  nand nand_28 (nand_28_out, xor_3_out, nand_31_out, nand_30_out);
  nand nand_29 (nand_29_out, eeprom_8kx16_1_out_2[8], eeprom_8kx16_1_out_2[8]);
  Register #(.width(1)) register_9 (.D(nor_6_out), .en(1'b1), .Q(register_9_q), .clk(CLK_out), .clr(RES_out));
  not not_23 (not_23_out, and_19_out);
  and and_19 (and_19_out, STATE[4], nor_5_out);
  nor nor_5 (nor_5_out, STATE[2], STATE[3], STATE[5], STATE[6]);
  nor nor_6 (nor_6_out, STATE[4], STATE[5], STATE[6]);
  nand nand_30 (nand_30_out, eeprom_8kx16_1_out_2[15], eeprom_8kx16_1_out_2[15]);
  nand nand_31 (nand_31_out, eeprom_8kx16_1_out_2[14], eeprom_8kx16_1_out_2[14]);
  REGISTER_FLAG register_flag_1 (
    .IN(mc_alu_8b_1_flag), .WRT(register_9_q), .CLK(CLK_out), .RST(RES_out), .OUT(register_flag_1_out));
  or or_9 (or_9_out, nor_6_out, and_17_out);
  xor xor_3 (xor_3_out, or_4_out, register_flag_1_out[0]);
  xor xor_4 (xor_4_out, or_4_out, register_flag_1_out[1]);
  MC_ALU_8B mc_alu_8b_1 (
    .DAT(buffer_8b_nts_2_q), .A_ISO(eeprom_8kx16_1_out_2[7]), .A_RW(eeprom_8kx16_1_out_2[9]),
    .SWP(and_19_out), .B_RW(not_23_out), .Start(or_9_out), .CMD_ISO(1'b1), .CMD_RW(eeprom_8kx16_1_out_2[8]),
    .CLK(CLK_out), .RST(RES_out), .Flag(mc_alu_8b_1_flag), .CMD_In(buffer_8b_nts_2_q),
    .CMD_Out(buffer_8b_nts_2_q), .DAT_O(buffer_8b_nts_2_q), .SEN_ACC1(A1), .SEN_ACC0(A0), .SEN_B1(B1),
    .SEN_B0(B0));  // open: Done, Z
  not not_24 (not_24_out, or_4_out);
  xor xor_5 (xor_5_out, or_4_out, register_flag_1_out[3]);
  nor nor_7 (nor_7_out, STATE[1], STATE[4], STATE[6]);
  not not_25 (not_25_out, STATE[0]);
  and and_20 (and_20_out, not_24_out, and_23_out);
  and and_21 (and_21_out, or_4_out, and_23_out);
  not not_26 (not_26_out, or_4_out);
  and and_22 (and_22_out, and_32_out, STATE[0]);
  and and_23 (and_23_out, nor_7_out, STATE[2], STATE[3], STATE[5]);
  and and_24 (and_24_out, not_25_out, and_20_out);
  and and_25 (and_25_out, and_20_out, STATE[0]);
  and and_26 (and_26_out, not_25_out, and_21_out);
  and and_27 (and_27_out, and_21_out, STATE[0]);
  PTRREG_16B ptrreg_16b_1 (
    .in_1(buffer_8b_nts_2_q), .CLK(CLK_out), .RST(RES_out), .Q({GP3, GP2, GP1, GP0}), .S0(and_30_out),
    .S1(and_34_out), .S2(and_31_out), .S3(and_22_out), .N(or_4_out));
  and and_28 (and_28_out, not_26_out, and_22_out);
  assign buffer_8b_nts_2_q = and_28_out ? {GP1, GP0} : 8'bz;  // Controlled_Buffer controlled_buffer_5
  and and_29 (and_29_out, or_4_out, and_22_out);
  assign buffer_8b_nts_2_q = and_29_out ? {GP3, GP2} : 8'bz;  // Controlled_Buffer controlled_buffer_6
  DotMatrix #(.matrixcols(8), .matrixrows(1)) dotmatrix_1 (
    .col0(port_ext_1_odat_o[7]), .col1(port_ext_1_odat_o[6]), .col2(port_ext_1_odat_o[5]),
    .col3(port_ext_1_odat_o[4]), .col4(port_ext_1_odat_o[3]), .col5(port_ext_1_odat_o[2]),
    .col6(port_ext_1_odat_o[1]), .col7(port_ext_1_odat_o[0]));
  PORT_EXT port_ext_1 (
    .IDAT_I(buffer_8b_nts_2_q), .WRT(and_24_out), .CLK(CLK_out), .RST(RES_out), .READ(and_25_out),
    .IDAT_O(buffer_8b_nts_2_q), .ODAT_O(port_ext_1_odat_o), .ODAT_I(in_1));
  DotMatrix #(.matrixcols(8), .matrixrows(1)) dotmatrix_2 (
    .col0(port_ext_2_odat_o[7]), .col1(port_ext_2_odat_o[6]), .col2(port_ext_2_odat_o[5]),
    .col3(port_ext_2_odat_o[4]), .col4(port_ext_2_odat_o[3]), .col5(port_ext_2_odat_o[2]),
    .col6(port_ext_2_odat_o[1]), .col7(port_ext_2_odat_o[0]));
  PORT_EXT port_ext_2 (
    .IDAT_I(buffer_8b_nts_2_q), .WRT(and_26_out), .CLK(CLK_out), .RST(RES_out), .READ(and_27_out),
    .IDAT_O(buffer_8b_nts_2_q), .ODAT_O(port_ext_2_odat_o), .ODAT_I(in_2));
  assign controlled_buffer_7_out = and_30_out ? buffer_8b_nts_2_q : 8'bz;  // Controlled_Buffer controlled_buffer_7
  Multiplexer #(.width(16), .enable("false")) multiplexer_2 (
    .in0({16{1'b1}}), .in1({GP3, GP2, GP1, GP0}), .out(multiplexer_2_out), .sel(and_30_out));
  and and_30 (and_30_out, not_27_out, and_33_out);
  and and_31 (and_31_out, not_27_out, and_32_out);
  and and_32 (and_32_out, STATE[1], and_35_out);
  and and_33 (and_33_out, not_28_out, and_35_out);
  not not_27 (not_27_out, STATE[0]);
  nor nor_8 (nor_8_out, STATE[2], STATE[3], STATE[6]);
  not not_28 (not_28_out, STATE[1]);
  not not_29 (not_29_out, and_30_out);
  and and_34 (and_34_out, and_33_out, STATE[0]);
  and and_35 (and_35_out, nor_8_out, and_36_out);
  and and_36 (and_36_out, STATE[4], STATE[5]);
  Button RST (.out(RST_out));
  RAM #(.addrWidth(16)) ram_2 (
    .addr(multiplexer_2_out), .data(controlled_buffer_7_out), .sel(1'b1), .clk(CLK_out), .ld(not_29_out),
    .clr(RST_out));

  // Notes on the sheet:
  //   Accumulator
  //   B
  //   Bit 6
  //   Bit 7
  //   GPREG 1
  //   GPREG 1
  //   GPR 0
  //   GPR 1
  //   Program Counter
  //   FETCH
  //   END
  //   Stack Pointer
  //   JMP
  //   NxtAdr
  //   Graphics Pointer
  //   S3
  //   S0
  //   S2
  //   S1
endmodule

module PORT_EXT (
  input  [7:0] IDAT_I,
  input  WRT,
  input  [7:0] ODAT_I,
  input  CLK,
  input  RST,
  input  READ,
  output [7:0] ODAT_O,
  output [7:0] IDAT_O
);

  wire buffer_1_out, not_1_out, not_2_out;
  wire [7:0] buffer_8b_nts_1_q, not_3_out, register_1_q;

  buf buffer_1 (buffer_1_out, WRT);
  Buffer_8B_NTS buffer_8b_nts_1 (.D(IDAT_I), .T(not_1_out), .Q(buffer_8b_nts_1_q));
  not not_1 (not_1_out, WRT);
  not not_2 (not_2_out, READ);
  Buffer_8B_NTS buffer_8b_nts_2 (.D(ODAT_I), .T(not_2_out), .Q(IDAT_O));
  Buffer_8B_NTS buffer_8b_nts_3 (.D(register_1_q), .T(buffer_1_out), .Q(buffer_8b_nts_1_q));
  Register register_1 (.D(buffer_8b_nts_1_q), .en(1'b1), .Q(register_1_q), .clk(CLK), .clr(RST));
  assign not_3_out = ~register_1_q;  // NOT_Gate not_3, 8 bits wide
  Pull_Resistor #(.pull(1)) pull_resistor_1 (.node(ODAT_I[7]));
  Transistor #(.\type ("n")) transistor_1 (.in(1'b0), .out(ODAT_I[7]), .gate(not_3_out[7]));
  Pull_Resistor #(.pull(1)) pull_resistor_2 (.node(ODAT_I[6]));
  Transistor #(.\type ("n")) transistor_2 (.in(1'b0), .out(ODAT_I[6]), .gate(not_3_out[6]));
  Pull_Resistor #(.pull(1)) pull_resistor_3 (.node(ODAT_I[4]));
  Pull_Resistor #(.pull(1)) pull_resistor_4 (.node(ODAT_I[5]));
  Transistor #(.\type ("n")) transistor_3 (.in(1'b0), .out(ODAT_I[4]), .gate(not_3_out[4]));
  Transistor #(.\type ("n")) transistor_4 (.in(1'b0), .out(ODAT_I[5]), .gate(not_3_out[5]));
  Pull_Resistor #(.pull(1)) pull_resistor_5 (.node(ODAT_I[2]));
  Pull_Resistor #(.pull(1)) pull_resistor_6 (.node(ODAT_I[3]));
  Transistor #(.\type ("n")) transistor_5 (.in(1'b0), .out(ODAT_I[3]), .gate(not_3_out[3]));
  Transistor #(.\type ("n")) transistor_6 (.in(1'b0), .out(ODAT_I[2]), .gate(not_3_out[2]));
  Pull_Resistor #(.pull(1)) pull_resistor_7 (.node(ODAT_I[1]));
  Transistor #(.\type ("n")) transistor_7 (.in(1'b0), .out(ODAT_I[1]), .gate(not_3_out[1]));
  Pull_Resistor #(.pull(1)) pull_resistor_8 (.node(ODAT_I[0]));
  Transistor #(.\type ("n")) transistor_8 (.in(1'b0), .out(ODAT_I[0]), .gate(not_3_out[0]));

  assign ODAT_O = ODAT_I;
endmodule

module PTRREG_16B (
  input  [7:0] in_1,
  input  S3,
  input  S2,
  input  S1,
  input  S0,
  input  N,
  input  CLK,
  input  RST,
  output [15:0] Q
);

  wire and_1_out, and_2_out, and_3_out, and_4_out, and_5_out, and_6_out, n73163_4b_counter_2_rco,
       n73163_4b_counter_3_rco, n73163_4b_counter_4_rco, not_1_out, not_2_out, or_1_out, or_2_out,
       register_1_q;

  Register #(.width(1)) register_1 (.D(S1), .en(1'b1), .Q(register_1_q), .clk(CLK), .clr(RST));
  not not_1 (not_1_out, S3);
  and and_1 (and_1_out, not_1_out, or_1_out);
  not not_2 (not_2_out, or_1_out);
  or or_1 (or_1_out, register_1_q, N);
  or or_2 (or_2_out, S1, S2);
  and and_2 (and_2_out, S0, not_2_out);
  and and_3 (and_3_out, not_2_out, or_2_out);
  and and_4 (and_4_out, n73163_4b_counter_4_rco, and_2_out, n73163_4b_counter_3_rco, n73163_4b_counter_2_rco);
  and and_5 (and_5_out, and_2_out, n73163_4b_counter_4_rco, n73163_4b_counter_3_rco);
  and and_6 (and_6_out, and_2_out, n73163_4b_counter_4_rco);
  _73163_4B_Counter u_73163_4b_counter_1 (
    .Down(and_1_out), .D(in_1[7:4]), .minus_LD(and_4_out), .CLK(CLK), .RST(RST), .Q(Q[15:12]));  // open: RCO
  _73163_4B_Counter u_73163_4b_counter_2 (
    .Down(and_1_out), .D(in_1[3:0]), .minus_LD(and_5_out), .CLK(CLK), .RST(RST), .Q(Q[11:8]),
    .RCO(n73163_4b_counter_2_rco));
  _73163_4B_Counter u_73163_4b_counter_3 (
    .Down(and_3_out), .D(in_1[7:4]), .minus_LD(and_6_out), .CLK(CLK), .RST(RST), .Q(Q[7:4]),
    .RCO(n73163_4b_counter_3_rco));
  _73163_4B_Counter u_73163_4b_counter_4 (
    .Down(and_3_out), .D(in_1[3:0]), .minus_LD(and_2_out), .CLK(CLK), .RST(RST), .Q(Q[3:0]),
    .RCO(n73163_4b_counter_4_rco));

  // Notes on the sheet:
  //   3
  //   2
  //   1
  //   0
endmodule
