// Logisim project CPU_1.circ as structural Verilog: 2 circuits, main circuit main
module main (
  input  s0,
  input  s1,
  input  s2,
  input  s3,
  input  B3,
  input  a3,
  input  b2,
  input  a2,
  input  b1,
  input  a1,
  input  b0,
  input  a0,
  input  M,
  input  Cn,
  output G,
  output Cn4,
  output P,
  output F3,
  output F2,
  output equ,
  output F1,
  output F0
);

  wire and_1_out, and_2_out, and_3_out, and_4_out, and_5_out, and_6_out, and_7_out, and_8_out, and_9_out,
       and_10_out, and_11_out, and_12_out, and_13_out, and_14_out, and_15_out, and_16_out, and_17_out,
       and_18_out, and_19_out, and_20_out, and_21_out, and_22_out, and_23_out, and_24_out, and_25_out,
       and_26_out, and_27_out, and_28_out, and_29_out, and_30_out, and_31_out, and_32_out, nand_1_out,
       nand_3_out, nor_1_out, nor_2_out, nor_3_out, nor_4_out, nor_5_out, nor_6_out, nor_7_out, nor_8_out,
       nor_10_out, nor_11_out, nor_12_out, not_1_out, not_2_out, not_3_out, not_4_out, not_5_out, not_6_out,
       not_7_out, not_8_out, not_9_out;

  not not_1 (not_1_out, B3);
  not not_2 (not_2_out, b2);
  not not_3 (not_3_out, b1);
  not not_4 (not_4_out, b0);
  and and_1 (and_1_out, B3, s3, a3);
  and and_2 (and_2_out, a3, s2, not_1_out);
  and and_3 (and_3_out, not_1_out, s1);
  and and_4 (and_4_out, B3, s0);
  and and_5 (and_5_out, b2, s3, a2);
  and and_6 (and_6_out, a2, s2, not_2_out);
  and and_7 (and_7_out, not_2_out, s1);
  and and_8 (and_8_out, b2, s0);
  and and_9 (and_9_out, b1, s3, a1);
  and and_10 (and_10_out, a1, s2, not_3_out);
  and and_11 (and_11_out, not_3_out, s1);
  and and_12 (and_12_out, b1, s0);
  and and_13 (and_13_out, b0, s3, a0);
  and and_14 (and_14_out, a0, s2, not_4_out);
  and and_15 (and_15_out, not_4_out, s1);
  and and_16 (and_16_out, b0, s0);
  nor nor_1 (nor_1_out, and_1_out, and_2_out);
  nor nor_2 (nor_2_out, and_3_out, and_4_out, a3);
  nor nor_3 (nor_3_out, and_5_out, and_6_out);
  nor nor_4 (nor_4_out, and_7_out, and_8_out, a2);
  nor nor_5 (nor_5_out, and_9_out, and_10_out);
  nor nor_6 (nor_6_out, and_11_out, and_12_out, a1);
  nor nor_7 (nor_7_out, and_13_out, and_14_out);
  nor nor_8 (nor_8_out, and_15_out, and_16_out, a0);
  not not_5 (not_5_out, M);
  and and_17 (and_17_out, nor_1_out, nor_4_out);
  and and_18 (and_18_out, nor_1_out, nor_3_out, nor_6_out);
  and and_19 (and_19_out, nor_1_out, nor_3_out, nor_5_out, nor_8_out);
  not not_6 (not_6_out, nor_2_out);
  and and_20 (and_20_out, nor_3_out, nor_5_out, nor_7_out, Cn, not_5_out);
  and and_21 (and_21_out, nor_3_out, nor_5_out, nor_8_out, not_5_out);
  and and_22 (and_22_out, nor_3_out, nor_6_out, not_5_out);
  and and_23 (and_23_out, nor_4_out, not_5_out);
  not not_7 (not_7_out, nor_4_out);
  and and_24 (and_24_out, nor_5_out, nor_7_out, Cn, not_5_out);
  and and_25 (and_25_out, nor_5_out, nor_8_out, not_5_out);
  and and_26 (and_26_out, nor_6_out, not_5_out);
  not not_8 (not_8_out, nor_6_out);
  and and_27 (and_27_out, Cn, nor_7_out, not_5_out);
  and and_28 (and_28_out, nor_8_out, not_5_out);
  not not_9 (not_9_out, nor_8_out);
  nand nand_1 (nand_1_out, nor_1_out, nor_3_out, nor_5_out, nor_7_out, Cn);
  nand nand_2 (P, nor_7_out, nor_5_out, nor_3_out, nor_1_out);
  nand nand_3 (nand_3_out, not_5_out, Cn);
  nor nor_9 (G, nor_2_out, and_17_out, and_18_out, and_19_out);
  and and_29 (and_29_out, nor_1_out, not_6_out);
  nor nor_10 (nor_10_out, and_20_out, and_21_out, and_22_out, and_23_out);
  and and_30 (and_30_out, nor_3_out, not_7_out);
  nor nor_11 (nor_11_out, and_24_out, and_25_out, and_26_out);
  and and_31 (and_31_out, nor_5_out, not_8_out);
  nor nor_12 (nor_12_out, and_27_out, and_28_out);
  and and_32 (and_32_out, nor_7_out, not_9_out);
  nand nand_4 (Cn4, G, nand_1_out);
  xor xor_1 (F3, and_29_out, nor_10_out);
  xor xor_2 (F2, and_30_out, nor_11_out);
  xor xor_3 (F1, and_31_out, nor_12_out);
  xor xor_4 (F0, and_32_out, nand_3_out);
  and and_33 (equ, F2, F3, F1, F0);
endmodule

module ALU (
);

  main main_1 ();  // open: s0, s1, s2, s3, B3, G, Cn4, a3, P, b2, F3, a2, b1, F2, equ, a1, b0, F1, F0, a0, M, Cn
endmodule
